// Logisim project alu.circ as structural Verilog: 12 circuits, main circuit alu
module alu (
  input  [31:0] A,
  input  [31:0] B,
  input  [3:0] ALUSel,
  output [31:0] Result
);

  wire [31:0] add0, and0, bsel0, mul0, mulh0, mulhu0, or0, sll0, slt0, sra0, srl0, sub0, xor0;

  Adder #(.width(32)) adder_1 (.a(A), .b(B), .out(add0));  // open: cin, cout
  Subtractor #(.width(32)) subtractor_1 (.a(A), .b(B), .out(sub0));  // open: bin, bout
  and_for_me and_for_me_1 (.in_1(A), .in_2(B), .out_3(and0));
  or_for_me or_for_me_1 (.in_1(A), .in_2(B), .out_3(or0));
  my_xor my_xor_1 (.in_1(A), .in_2(B), .out_3(xor0));
  my_srl my_srl_1 (.in_1(A), .in_2(B), .out_3(srl0));
  my_sra my_sra_1 (.in_1(A), .in_2(B), .out_3(sra0));
  my_sll my_sll_1 (.in_1(A), .in_2(B), .out_3(sll0));
  my_slt my_slt_1 (.in_1(A), .in_2(B), .out_3(slt0));
  my_mul my_mul_1 (.in_1(A), .in_2(B), .out_3(mul0));
  my_mulhu my_mulhu_1 (.in_1(A), .in_2(B), .out_3(mulhu0));
  my_mulh my_mulh_1 (.in_1(A), .in_2(B), .out_3(mulh0));
  my_bsel my_bsel_1 (.in_1(A), .in_2(B), .out_3(bsel0));
  Multiplexer #(.enable("false"), .select(4), .width(32)) multiplexer_1 (
    .in0(add0), .in1(and0), .in2(or0), .in3(xor0), .in4(srl0), .in5(sra0), .in6(sll0), .in7(slt0),
    .in10(mul0), .in11(mulhu0), .in12(sub0), .in13(bsel0), .in14(mulh0), .out(Result), .sel(ALUSel));  // open: in8, in9, in15

  // Notes on the sheet:
  //   INPUTS to your circuit
  //   DON'T CHANGE THE LOCATIONS OF THE INPUTS AND OUTPUTS!
  //   OUTPUT from your circuit
endmodule

module and_for_me (
  input  [31:0] in_1,
  input  [31:0] in_2,
  output [31:0] out_3
);

  assign out_3 = in_1 & in_2;  // AND_Gate and_1, 32 bits wide
endmodule

module or_for_me (
  input  [31:0] in_1,
  input  [31:0] in_2,
  output [31:0] out_3
);

  assign out_3 = in_1 | in_2;  // OR_Gate or_1, 32 bits wide
endmodule

module my_xor (
  input  [31:0] in_1,
  input  [31:0] in_2,
  output [31:0] out_3
);

  assign out_3 = in_1 ^ in_2;  // XOR_Gate xor_1, 32 bits wide
endmodule

module my_srl (
  input  [31:0] in_1,
  input  [31:0] in_2,
  output [31:0] out_3
);

  Shifter #(.shift("lr"), .width(32)) shifter_1 (.in(in_1), .\dist (in_2[4:0]), .out(out_3));
endmodule

module my_sra (
  input  [31:0] in_1,
  input  [31:0] in_2,
  output [31:0] out_3
);

  Shifter #(.shift("ar"), .width(32)) shifter_1 (.in(in_1), .\dist (in_2[4:0]), .out(out_3));
endmodule

module my_sll (
  input  [31:0] in_1,
  input  [31:0] in_2,
  output [31:0] out_3
);

  Shifter #(.width(32)) shifter_1 (.in(in_1), .\dist (in_2[4:0]), .out(out_3));
endmodule

module my_slt (
  input  [31:0] in_1,
  input  [31:0] in_2,
  output [31:0] out_3
);

  wire comparator_1_lt;

  Comparator #(.width(32)) comparator_1 (.a(in_1), .b(in_2), .lt(comparator_1_lt));  // open: gt, eq
  assign out_3 = {{31{1'b0}}, comparator_1_lt};  // Bit_Extender bit_extender_1
endmodule

module my_mul (
  input  [31:0] in_1,
  input  [31:0] in_2,
  output [31:0] out_3
);

  Multiplier #(.mode("twosComplement"), .width(32)) multiplier_1 (.a(in_1), .b(in_2), .out(out_3));  // open: cin, cout
endmodule

module my_mulhu (
  input  [31:0] in_1,
  input  [31:0] in_2,
  output [31:0] out_3
);

  Multiplier #(.width(32)) multiplier_1 (.a(in_1), .b(in_2), .cout(out_3));  // open: out, cin
endmodule

module my_mulh (
  input  [31:0] in_1,
  input  [31:0] in_2,
  output [31:0] out_3
);

  Multiplier #(.mode("twosComplement"), .width(32)) multiplier_1 (.a(in_1), .b(in_2), .cout(out_3));  // open: out, cin
endmodule

module my_bsel (
  input  [31:0] in_1,
  input  [31:0] in_2,
  output [31:0] out_3
);


  assign out_3 = in_2;
endmodule
