// Logisim project control_logic.circ as structural Verilog: 1 circuit, main circuit control_logic
module control_logic (
  input  [31:0] inst,
  input  BrEq,
  input  BrLt,
  output PCSel,
  output RegWEn,
  output [2:0] ImmSel,
  output BrUn,
  output ASel,
  output BSel,
  output [3:0] ALUSel,
  output MemRW,
  output [1:0] WBSel,
  output CSRSel,
  output CSRWen
);

  wire and_1_out, and_2_out, and_3_out, is_I_type, is_I_type1, is_I_type2, is_I_type3, is_I_type4, is_R_type,
       is_S_type, is_SB_type, is_U_type, is_U_type1, is_U_type2, is_UJ_type, not_1_out, or_3_out;

  Comparator #(.width(7)) comparator_1 (.a(inst[6:0]), .b(7'b0110011), .eq(is_R_type));  // open: gt, lt
  Comparator #(.width(7)) comparator_2 (.a(inst[6:0]), .b(7'b0000011), .eq(is_I_type1));  // open: gt, lt
  Comparator #(.width(7)) comparator_3 (.a(inst[6:0]), .b(7'b0010011), .eq(is_I_type2));  // open: gt, lt
  Comparator #(.width(7)) comparator_4 (.a(inst[6:0]), .b(7'b0010111), .eq(is_U_type1));  // open: gt, lt
  Comparator #(.width(7)) comparator_5 (.a(inst[6:0]), .b(7'b0110111), .eq(is_U_type2));  // open: gt, lt
  Comparator #(.width(7)) comparator_6 (.a(inst[6:0]), .b(7'b1101111), .eq(is_UJ_type));  // open: gt, lt
  Comparator #(.width(7)) comparator_7 (.a(inst[6:0]), .b(7'b0100011), .eq(is_S_type));  // open: gt, lt
  Comparator #(.width(7)) comparator_8 (.a(inst[6:0]), .b(7'b1100011), .eq(is_SB_type));  // open: gt, lt
  or or_1 (BSel, is_UJ_type, is_U_type, is_I_type);
  or or_2 (is_U_type, is_U_type1, is_U_type2);
  or or_3 (or_3_out, is_UJ_type, is_U_type);
  not not_1 (not_1_out, inst[13]);
  and and_1 (and_1_out, inst[12], not_1_out);
  and and_2 (and_2_out, and_1_out, inst[14]);
  Comparator #(.width(7)) comparator_9 (.a(inst[6:0]), .b(7'b1100111), .eq(is_I_type3));  // open: gt, lt
  Comparator #(.width(7)) comparator_10 (.a(inst[6:0]), .b(7'b1110011), .eq(is_I_type4));  // open: gt, lt
  and and_3 (and_3_out, and_2_out, is_I_type4);
  or or_4 (RegWEn, is_I_type, is_U_type2, is_U_type1, is_UJ_type, is_R_type);
  or or_5 (is_I_type, is_I_type1, is_I_type2, is_I_type3, is_I_type4);
  or or_6 (ASel, or_3_out, and_3_out);

  assign ALUSel = 4'b0000;
  assign BrUn = 1'b0;
  assign ImmSel = 3'b000;
  assign PCSel = 1'b0;

  // Other names for the same wires on the sheet: opcode[6:0] = inst[6:0]; funct3[2:0] = inst[14:12];
  //   funct7[6:0] = inst[31:25]

  // Notes on the sheet:
  //   INPUTS to your circuit
  //   DON'T CHANGE THE LOCATIONS OF THE INPUTS AND OUTPUTS!
  //   OUTPUT from your circuit
endmodule
