// Logisim project regfile.circ as structural Verilog: 2 circuits, main circuit regfile
module regfile (
  input  [4:0] rs1,
  input  [4:0] rs2,
  input  [4:0] rd,
  input  [31:0] Write_Data,
  input  RegWEn,
  input  clk,
  input  in_7,
  output [31:0] ra,
  output [31:0] sp,
  output [31:0] t0,
  output [31:0] t1,
  output [31:0] t2,
  output [31:0] s0,
  output [31:0] s1,
  output [31:0] a0,
  output [31:0] Read_Data_1,
  output [31:0] Read_Data_2
);

  wire demultiplexer_1_out0, we1, we2, we3, we4, we5, we6, we7, we8, we9, we10, we11, we12, we13, we14, we15,
       we16, we17, we18, we19, we20, we21, we22, we23, we24, we25, we26, we27, we28, we29, we30, we31, we32;
  wire [31:0] r1_1, r1_4, r1_5, r1_12, r1_13, r1_14, r1_15, r1_16, r1_17, r1_18, r1_19, r1_20, r1_21, r1_22,
       r1_23, r1_24, r1_25, r1_26, r1_27, r1_28, r1_29, r1_30, r1_31, r1_32;

  Multiplexer #(.enable("false"), .select(5), .width(32)) multiplexer_1 (
    .in0(r1_1), .in1(ra), .in2(sp), .in3(r1_4), .in4(r1_5), .in5(t0), .in6(t1), .in7(t2), .in8(s0), .in9(s1),
    .in10(a0), .in11(r1_12), .in12(r1_13), .in13(r1_14), .in14(r1_15), .in15(r1_16), .in16(r1_17),
    .in17(r1_18), .in18(r1_19), .in19(r1_20), .in20(r1_21), .in21(r1_22), .in22(r1_23), .in23(r1_24),
    .in24(r1_25), .in25(r1_26), .in26(r1_27), .in27(r1_28), .in28(r1_29), .in29(r1_30), .in30(r1_31),
    .in31(r1_32), .out(Read_Data_1), .sel(rs1));
  xten xten_1 (.in_1(Write_Data), .we(we1), .in_3(clk), .out_4(r1_1));
  xten xten_2 (.in_1(Write_Data), .we(we2), .in_3(clk), .out_4(ra));
  xten xten_3 (.in_1(Write_Data), .we(we3), .in_3(clk), .out_4(sp));
  xten xten_4 (.in_1(Write_Data), .we(we4), .in_3(clk), .out_4(r1_4));
  xten xten_5 (.in_1(Write_Data), .we(we5), .in_3(clk), .out_4(r1_5));
  xten xten_6 (.in_1(Write_Data), .we(we6), .in_3(clk), .out_4(t0));
  xten xten_7 (.in_1(Write_Data), .we(we7), .in_3(clk), .out_4(t1));
  xten xten_8 (.in_1(Write_Data), .we(we8), .in_3(clk), .out_4(t2));
  xten xten_9 (.in_1(Write_Data), .we(we9), .in_3(clk), .out_4(s0));
  xten xten_10 (.in_1(Write_Data), .we(we10), .in_3(clk), .out_4(s1));
  xten xten_11 (.in_1(Write_Data), .we(we11), .in_3(clk), .out_4(a0));
  xten xten_12 (.in_1(Write_Data), .we(we12), .in_3(clk), .out_4(r1_12));
  xten xten_13 (.in_1(Write_Data), .we(we13), .in_3(clk), .out_4(r1_13));
  xten xten_14 (.in_1(Write_Data), .we(we14), .in_3(clk), .out_4(r1_14));
  xten xten_15 (.in_1(Write_Data), .we(we15), .in_3(clk), .out_4(r1_15));
  xten xten_16 (.in_1(Write_Data), .we(we16), .in_3(clk), .out_4(r1_16));
  Multiplexer #(.enable("false"), .select(5), .width(32)) multiplexer_2 (
    .in0(r1_1), .in1(ra), .in2(sp), .in3(r1_4), .in4(r1_5), .in5(t0), .in6(t1), .in7(t2), .in8(s0), .in9(s1),
    .in10(a0), .in11(r1_12), .in12(r1_13), .in13(r1_14), .in14(r1_15), .in15(r1_16), .in16(r1_17),
    .in17(r1_18), .in18(r1_19), .in19(r1_20), .in20(r1_21), .in21(r1_22), .in22(r1_23), .in23(r1_24),
    .in24(r1_25), .in25(r1_26), .in26(r1_27), .in27(r1_28), .in28(r1_29), .in29(r1_30), .in30(r1_31),
    .in31(r1_32), .out(Read_Data_2), .sel(rs2));
  xten xten_17 (.in_1(Write_Data), .we(we17), .in_3(clk), .out_4(r1_17));
  xten xten_18 (.in_1(Write_Data), .we(we18), .in_3(clk), .out_4(r1_18));
  xten xten_19 (.in_1(Write_Data), .we(we19), .in_3(clk), .out_4(r1_19));
  xten xten_20 (.in_1(Write_Data), .we(we20), .in_3(clk), .out_4(r1_20));
  xten xten_21 (.in_1(Write_Data), .we(we21), .in_3(clk), .out_4(r1_21));
  xten xten_22 (.in_1(Write_Data), .we(we22), .in_3(clk), .out_4(r1_22));
  xten xten_23 (.in_1(Write_Data), .we(we23), .in_3(clk), .out_4(r1_23));
  xten xten_24 (.in_1(Write_Data), .we(we24), .in_3(clk), .out_4(r1_24));
  xten xten_25 (.in_1(Write_Data), .we(we25), .in_3(clk), .out_4(r1_25));
  xten xten_26 (.in_1(Write_Data), .we(we26), .in_3(clk), .out_4(r1_26));
  xten xten_27 (.in_1(Write_Data), .we(we27), .in_3(clk), .out_4(r1_27));
  xten xten_28 (.in_1(Write_Data), .we(we28), .in_3(clk), .out_4(r1_28));
  xten xten_29 (.in_1(Write_Data), .we(we29), .in_3(clk), .out_4(r1_29));
  xten xten_30 (.in_1(Write_Data), .we(we30), .in_3(clk), .out_4(r1_30));
  xten xten_31 (.in_1(Write_Data), .we(we31), .in_3(clk), .out_4(r1_31));
  xten xten_32 (.in_1(Write_Data), .we(we32), .in_3(clk), .out_4(r1_32));
  Demultiplexer #(.enable("false"), .select(5)) demultiplexer_1 (
    .out0(demultiplexer_1_out0), .out1(we2), .out2(we3), .out3(we4), .out4(we5), .out5(we6), .out6(we7),
    .out7(we8), .out8(we9), .out9(we10), .out10(we11), .out11(we12), .out12(we13), .out13(we14),
    .out14(we15), .out15(we16), .out16(we17), .out17(we18), .out18(we19), .out19(we20), .out20(we21),
    .out21(we22), .out22(we23), .out23(we24), .out24(we25), .out25(we26), .out26(we27), .out27(we28),
    .out28(we29), .out29(we30), .out30(we31), .out31(we32), .in(RegWEn), .sel(rd));
  and and_1 (we1, in_7, demultiplexer_1_out0);

  // Other names for the same wires on the sheet: r2_1[31:0] = r1_1; r1_2[31:0] = ra; r2_2[31:0] = ra; r1_3[31:0] = sp;
  //   r2_3[31:0] = sp; r2_4[31:0] = r1_4; r2_5[31:0] = r1_5; r1_6[31:0] = t0; r2_6[31:0] = t0; r1_7[31:0] = t1;
  //   r2_7[31:0] = t1; r1_8[31:0] = t2; r2_8[31:0] = t2; r1_9[31:0] = s0; r2_9[31:0] = s0; r1_10[31:0] = s1;
  //   r2_10[31:0] = s1; r1_11[31:0] = a0; r2_11[31:0] = a0; r2_12[31:0] = r1_12; r2_13[31:0] = r1_13;
  //   r2_14[31:0] = r1_14; r2_15[31:0] = r1_15; r2_16[31:0] = r1_16; r2_17[31:0] = r1_17; r2_18[31:0] = r1_18;
  //   r2_19[31:0] = r1_19; r2_20[31:0] = r1_20; r2_21[31:0] = r1_21; r2_22[31:0] = r1_22; r2_23[31:0] = r1_23;
  //   r2_24[31:0] = r1_24; r2_25[31:0] = r1_25; r2_26[31:0] = r1_26; r2_27[31:0] = r1_27; r2_28[31:0] = r1_28;
  //   r2_29[31:0] = r1_29; r2_30[31:0] = r1_30; r2_31[31:0] = r1_31; r2_32[31:0] = r1_32;
  //   read_data1[31:0] = Read_Data_1; read_data2[31:0] = Read_Data_2; read_reg1[4:0] = rs1; read_reg2[4:0] = rs2;
  //   write_en = RegWEn; write_reg[4:0] = rd

  // Notes on the sheet:
  //   INPUTS to your circuit
  //   DON'T CHANGE THE LOCATIONS OF THE INPUTS AND OUTPUTS!
  //   These are DEBUG/TEST outputs from your circuit.
  //   OUTPUTS from your circuit
endmodule

module xten (
  input  [31:0] in_1,
  input  we,
  input  in_3,
  output [31:0] out_4
);

  Register #(.width(32)) register_1 (.D(in_1), .en(we), .clk(in_3), .Q(out_4));  // open: clr
endmodule
